# Fritzing sketch e-schema (saved by Fritzing 0.9.3b)
breadboards: 2

parts:
  S1 = Pushbutton [package="[THT]"]
  S2 = Pushbutton [package="[THT]"]
  LED1 = LED - 5mm [color="Blue (470nm)" package="5 mm [THT]"]
  LED2 = LED - 5mm [color="Blue (470nm)" package="5 mm [THT]"]
  R1 = Resistor [tolerance=±5% resistance=220 package=THT]
  R2 = Resistor [tolerance=±5% resistance=220 package=THT]
  Part1 = Arduino Uno (Rev3)
  R3 = Resistor [tolerance=±5% resistance=10k package=THT]
  R4 = Resistor [tolerance=±5% resistance=10k package=THT]
  U1 = 74HC595 [package="DIP16 [THT]"]
  LED4 = LED - 5mm [color="Red (633nm)" package="5 mm [THT]"]
  R5 = Resistor [tolerance=±5% resistance=220 package=THT]
  S3 = Reed switch [package=THT]
  R6 = Resistor [tolerance=±5% resistance=10k package=THT]
  U2 = 7-SEGMENT-DISPLAY [package=7-segment-display]
  R7 = Resistor [tolerance=±5% resistance=220 package=THT]

nets:
  N1: S1.Pin_1, S1.Pin_2, Part1.D7, R3.Pin_0
  5V: S1.Pin_3, S1.Pin_4, S2.Pin_3, S2.Pin_4, Part1.5V, U1.MR, U1.VCC, S3.pin_1
  N2: S2.Pin_1, S2.Pin_2, Part1.D6_PWM, R4.Pin_0
  GND: LED1.cathode, LED2.cathode, Part1.GND, R3.Pin_1, R4.Pin_1, U1.GND, U1.OE, LED4.cathode, R6.Pin_1, R7.Pin_0
  N3: LED1.anode, R2.Pin_0
  N4: LED2.anode, R1.Pin_0
  N5: R1.Pin_1, Part1.D4
  N6: R2.Pin_1, Part1.D2
  N7: Part1.D8, U1.ST_CP
  N8: Part1.D9_PWM, R5.Pin_1
  N9: Part1.D11_PWM/MOSI, U1.DS
  N10: Part1.D12/MISO, U1.SH_CP
  N11: Part1.D13/SCK, S3.pin_2, R6.Pin_0
  N12: U1.Q1, U2.A
  N13: U1.Q2, U2.DP
  N14: U1.Q3, U2.G1
  N15: U1.Q4, U2.D
  N16: U1.Q5, U2.G
  N17: U1.Q6, U2.E
  N18: U1.Q7, U2.B
  N19: U1.Q0, U2.G2
  N20: LED4.anode, R5.Pin_0
  N21: U2.C, R7.Pin_1
